// Logisim project lookahead.circ as structural Verilog: 1 circuit, main circuit main
module main (
  input  CN,
  input  X0,
  input  Y0,
  input  X1,
  input  Y1,
  input  X2,
  input  Y2,
  input  X3,
  input  Y3,
  output S0,
  output C0,
  output S1,
  output C1,
  output S2,
  output C2,
  output S3,
  output C3
);

  wire and_1_out, and_2_out, and_3_out, and_4_out, and_5_out, and_6_out, and_7_out, and_8_out, and_9_out,
       and_10_out, G0_out, G1_out, G2_out, G3_out, or_3_out, or_6_out, or_7_out, or_9_out, or_11_out,
       or_12_out, P0_out, P1_out, P2_out, P3_out;

  xor P0 (P0_out, X0, Y0);
  and G0 (G0_out, X0, Y0);
  or or_1 (S0, CN, P0_out);
  and and_1 (and_1_out, CN, P0_out);
  xor xor_1 (C0, and_1_out, G0_out);
  xor P1 (P1_out, X1, Y1);
  and G1 (G1_out, X1, Y1);
  and and_2 (and_2_out, P1_out, G0_out);
  and and_3 (and_3_out, P1_out, P0_out, CN);
  or or_2 (S1, C0, P1_out);
  or or_3 (or_3_out, and_2_out, G1_out);
  or or_4 (C1, or_3_out, and_3_out);
  xor P2 (P2_out, X2, Y2);
  and G2 (G2_out, X2, Y2);
  or or_5 (S2, C1, P2_out);
  and and_4 (and_4_out, P2_out, G1_out);
  and and_5 (and_5_out, P2_out, P1_out, G0_out);
  or or_6 (or_6_out, G2_out, and_4_out);
  or or_7 (or_7_out, or_6_out, and_5_out);
  and and_6 (and_6_out, P2_out, P1_out, P0_out, CN);
  or or_8 (C2, or_7_out, and_6_out);
  xor P3 (P3_out, X3, Y3);
  and G3 (G3_out, X3, Y3);
  and and_7 (and_7_out, P3_out, G2_out);
  or or_9 (or_9_out, G3_out, and_7_out);
  and and_8 (and_8_out, P3_out, P2_out, G1_out);
  or or_10 (S3, C2, P3_out);
  or or_11 (or_11_out, or_9_out, and_8_out);
  and and_9 (and_9_out, P3_out, P2_out, P1_out, G0_out);
  or or_12 (or_12_out, or_11_out, and_9_out);
  and and_10 (and_10_out, P3_out, P2_out, P1_out, CN);
  or or_13 (C3, or_12_out, and_10_out);
endmodule
